# Fritzing sketch esquemaEletrico (saved by Fritzing 0.9.3b)
breadboards: 1

parts:
  MCU1 = Raspberry Pi Zero
  S1 = Pushbutton [package="[THT]"]
  LED1 = LED - 5mm [color="Red (633nm)" package="5 mm [THT]"]
  R1 = Resistor [tolerance=±5% resistance=220 package=THT]
  R2 = Resistor [tolerance=±5% resistance=220 package=THT]

nets:
  N1: MCU1.pin_1, S1.Pin_1, S1.Pin_2
  GND: MCU1.pin_9, MCU1.pin_20, MCU1.pin_30, MCU1.pin_39, R1.Pin_0, R2.Pin_0
  N2: MCU1.pin_13, LED1.anode
  N3: MCU1.pin_18, S1.Pin_3, S1.Pin_4, R2.Pin_1
  N4: LED1.cathode, R1.Pin_1
